# Fritzing sketch kaffezeit_schem (saved by Fritzing 0.9.2b)
breadboards: 1

parts:
  U1 = ESP8266 WiFi Module [part_number=ESP8266]
  Part1 = Arduino Uno (Rev3)
  KY-5 = Keyes Relay [package=THT]

nets:
  N1: U1.RXD, Part1.D1/TX
  VCC: U1.VCC, U1.CH_PD, Part1.3V3
  GND: U1.GND, Part1.GND, KY-5.ground
  N2: U1.TXD, Part1.D0/RX
  N3: Part1.D2, KY-5.signal
  N4: Part1.5V, KY-5.power

notes:
  CMN
  Coffee machine
  Find pin numbers on GGecko for:
  Tx to Rx
  Rx to Tx
  Neutral Coffee Machine
  VDD
  Coffee
  machine

custom parts:
  ESP8266 WiFi Module: Generic WiFi Module based on the ESP8266 with onboard PCB antenna and UART communications
  Keyes Relay: The Keyes 5V relay module is suitable for SCM development, home appliance control. It uses a 5V~12V TIL control signal which can control DC / AC signal.
